# Fritzing sketch mo (saved by Fritzing 0.9.3b)
breadboards: 1

parts:
  LED1 = LED - 5mm [color="Blue (470nm)" package="5 mm [THT]"]  # not connected
  LED2 = LED - 5mm [color="Blue (470nm)" package="5 mm [THT]"]
  LED3 = LED - 5mm [color="Yellow (595nm)" package="5 mm [THT]"]
  R1 = Resistor [tolerance=±5% resistance=330k package=THT]
  R2 = Resistor [tolerance=±5% resistance=330k package=THT]
  R3 = Resistor [tolerance=±5% resistance=330k package=THT]
  Part1 = Arduino Uno (Rev3)
  Part2 = Soil Moisture Sensor

nets:
  N1: LED2.cathode, LED3.cathode, R1.Pin_0
  N2: LED2.anode, R2.Pin_0
  N3: LED3.anode, R3.Pin_0
  N4: R1.Pin_1, Part1.D9_PWM
  N5: R2.Pin_1, Part1.D10_PWM/SS
  N6: R3.Pin_1, Part1.D11_PWM/MOSI
  N7: Part1.A0, Part2.SIG
  5V: Part1.5V, Part2.VCC
  GND: Part1.GND, Part2.GND
